// Logisim project cpu3.circ as structural Verilog: 7 circuits, main circuit main
module main (
);

  wire alu_1_carry, alu_1_zero, and_1_out, and_2_out, and_3_out, and_4_out, and_5_out, and_6_out, and_7_out,
       and_8_out, and_9_out, and_10_out, and_11_out, and_12_out, and_13_out, and_14_out, and_15_out,
       and_17_out, and_18_out, and_19_out, and_20_out, and_21_out, buffer_1_out, buffer_2_out, buffer_3_out,
       buffer_4_out, buffer_5_out, buffer_7_out, buffer_8_out, buffer_9_out, buffer_10_out, buffer_11_out,
       buffer_12_out, buffer_13_out, buffer_14_out, buffer_15_out, buffer_16_out, buffer_17_out,
       buffer_18_out, buffer_19_out, buffer_20_out, buffer_21_out, buffer_22_out, buffer_23_out,
       buffer_24_out, buffer_25_out, buffer_26_out, buffer_27_out, buffer_28_out, button_1_out, button_2_out,
       clock_1_out, controlled_buffer_2_out, controlled_buffer_6_out, controlled_buffer_14_out,
       controlled_buffer_17_out, controlled_buffer_27_out, controlled_buffer_28_out,
       controlled_buffer_29_out, d_ff_1_q, d_ff_1_qn, d_ff_2_q, d_ff_3_q, demultiplexer_1_out0,
       demultiplexer_1_out1, demultiplexer_1_out2, demultiplexer_1_out3, demultiplexer_2_out1,
       demultiplexer_2_out2, demultiplexer_2_out3, demultiplexer_2_out4, demultiplexer_2_out9,
       demultiplexer_2_out10, demultiplexer_2_out11, demultiplexer_2_out12, demultiplexer_2_out13,
       demultiplexer_2_out14, demultiplexer_2_out15, demultiplexer_2_out16, demultiplexer_2_out17,
       demultiplexer_2_out18, demultiplexer_4_out0, demultiplexer_4_out1, demultiplexer_4_out2,
       demultiplexer_4_out3, or_2_out, or_3_out, or_4_out, or_5_out, or_6_out, priority_encoder_1_p1,
       priority_encoder_1_p2, priority_encoder_1_p4, priority_encoder_1_p5, priority_encoder_2_p5,
       pull_resistor_1_node, pull_resistor_2_node, rgbled_1_p1;
  wire [1:0] buffer_6_out, counter_1_q, priority_encoder_1_p3, priority_encoder_2_p3;
  wire [2:0] bit_extender_1_out, controlled_buffer_21_out;
  wire [7:0] alu_1_sum, controlled_buffer_1_out, controlled_buffer_3_out, controlled_buffer_4_out,
       controlled_buffer_5_out, controlled_buffer_15_out, controlled_buffer_16_out, controlled_buffer_19_out,
       controlled_buffer_20_out, controlled_buffer_25_out, counter_2_q, mmu_1_out_11, multiplexer_1_out,
       multiplexer_2_out, pull_resistor_9_node, pull_resistor_10_node, pull_resistor_11_node, register_1_q,
       register_2_q, register_3_q, register_4_q, register_5_q, register_6_q, rom_1_data;
  wire [14:0] mmu_1_romaddr;

  D_Flip_Flop d_ff_1 (
    .D(and_5_out), .clk(and_5_out), .Q(d_ff_1_q), .Qn(d_ff_1_qn), .preset(button_2_out), .reset(button_1_out));
  Button button_1 (.out(button_1_out));
  Button button_2 (.out(button_2_out));
  Demultiplexer #(.select(2)) demultiplexer_1 (
    .out0(demultiplexer_1_out0), .out1(demultiplexer_1_out1), .out2(demultiplexer_1_out2),
    .out3(demultiplexer_1_out3), .in(and_1_out), .sel(counter_1_q));
  Counter #(.max('h2), .trigger("falling"), .width(2)) counter_1 (
    .Q(counter_1_q), .clk(buffer_1_out));  // open: load, D, count, carry, up, clr
  buf buffer_1 (buffer_1_out, and_1_out);
  and and_1 (and_1_out, ~d_ff_1_q, clock_1_out);  // AND_Gate
  Clock clock_1 (.out(clock_1_out));
  LED led_1 (.in(d_ff_1_qn));
  // RGBLED rgbled_1: pin names not known; wires that end beside it: rgbled_1_p1, demultiplexer_1_out0
  or or_1 (rgbled_1_p1, demultiplexer_1_out1, demultiplexer_1_out2);
  // NoConnect on demultiplexer_1_out3
  buf buffer_2 (buffer_2_out, buffer_3_out);
  buf buffer_3 (buffer_3_out, buffer_4_out);
  buf buffer_4 (buffer_4_out, buffer_5_out);
  buf buffer_5 (buffer_5_out, pull_resistor_1_node);
  Pull_Resistor pull_resistor_1 (.node(pull_resistor_1_node));
  assign controlled_buffer_1_out = demultiplexer_1_out0 ? counter_2_q : 8'bz;  // Controlled_Buffer controlled_buffer_1
  Counter #(.trigger("falling")) counter_2 (
    .load(buffer_2_out), .D(controlled_buffer_25_out), .Q(counter_2_q), .clk(or_2_out), .clr(and_4_out));  // open: count, carry, up
  or or_2 (or_2_out, demultiplexer_1_out0, or_3_out);
  or or_3 (or_3_out, pull_resistor_1_node, pull_resistor_2_node);
  Pull_Resistor pull_resistor_2 (.node(pull_resistor_2_node));
  Register #(.trigger("falling")) register_1 (
    .D(mmu_1_out_11), .Q(register_1_q), .clk(demultiplexer_1_out0));  // open: en, clr
  assign controlled_buffer_2_out = demultiplexer_1_out0 ? demultiplexer_1_out0 : 1'bz;  // Controlled_Buffer controlled_buffer_2
  assign buffer_6_out = register_1_q[6:5];  // Buffer buffer_6, 2 bits wide
  assign controlled_buffer_3_out = demultiplexer_2_out3 ? multiplexer_2_out : 8'bz;  // Controlled_Buffer controlled_buffer_3
  assign controlled_buffer_4_out = demultiplexer_2_out4 ? multiplexer_2_out : 8'bz;  // Controlled_Buffer controlled_buffer_4
  and and_2 (and_2_out, demultiplexer_1_out1, demultiplexer_2_out3);
  and and_3 (and_3_out, demultiplexer_1_out1, demultiplexer_2_out4);
  and and_4 (and_4_out, demultiplexer_2_out1, demultiplexer_1_out1);
  and and_5 (and_5_out, demultiplexer_2_out2, demultiplexer_1_out1);
  Multiplexer #(.select(2), .width(8)) multiplexer_1 (
    .in0(register_3_q), .in1(register_4_q), .in2(register_5_q), .in3(register_6_q), .out(multiplexer_1_out),
    .sel(priority_encoder_1_p3));
  assign controlled_buffer_5_out = and_6_out ? multiplexer_1_out : 8'bz;  // Controlled_Buffer controlled_buffer_5
  buf buffer_7 (buffer_7_out, and_6_out);
  buf buffer_8 (buffer_8_out, buffer_7_out);
  assign controlled_buffer_6_out = and_6_out ? buffer_8_out : 1'bz;  // Controlled_Buffer controlled_buffer_6
  and and_6 (and_6_out, demultiplexer_1_out1, or_4_out);
  or or_4 (or_4_out, priority_encoder_1_p1, priority_encoder_1_p2, priority_encoder_1_p4, priority_encoder_1_p5);
  buf buffer_9 (buffer_9_out, and_10_out);
  buf buffer_10 (buffer_10_out, buffer_9_out);
  buf buffer_11 (buffer_11_out, buffer_10_out);
  buf buffer_12 (buffer_12_out, buffer_11_out);
  assign controlled_buffer_2_out = and_10_out ? buffer_12_out : 1'bz;  // Controlled_Buffer controlled_buffer_7
  // Priority_Encoder #(.select(2)) priority_encoder_1: pin names not known; wires that end beside it: priority_encoder_1_p1, priority_encoder_1_p2, priority_encoder_1_p3, priority_encoder_1_p4, priority_encoder_1_p5
  Pull_Resistor pull_resistor_3 (.node(priority_encoder_1_p3));
  assign controlled_buffer_1_out = and_10_out ? counter_2_q : 8'bz;  // Controlled_Buffer controlled_buffer_8
  assign controlled_buffer_5_out = and_8_out ? mmu_1_out_11 : 8'bz;  // Controlled_Buffer controlled_buffer_9
  buf buffer_13 (buffer_13_out, and_8_out);
  buf buffer_14 (buffer_14_out, buffer_13_out);
  assign controlled_buffer_6_out = and_8_out ? buffer_14_out : 1'bz;  // Controlled_Buffer controlled_buffer_10
  and and_7 (and_7_out, rgbled_1_p1, ~register_1_q[7]);  // AND_Gate
  Demultiplexer #(.select(5)) demultiplexer_2 (
    .out1(demultiplexer_2_out1), .out2(demultiplexer_2_out2), .out3(demultiplexer_2_out3),
    .out4(demultiplexer_2_out4), .out5(priority_encoder_1_p1), .out6(priority_encoder_1_p2),
    .out7(priority_encoder_1_p4), .out8(priority_encoder_1_p5), .out9(demultiplexer_2_out9),
    .out10(demultiplexer_2_out10), .out11(demultiplexer_2_out11), .out12(demultiplexer_2_out12),
    .out13(demultiplexer_2_out13), .out14(demultiplexer_2_out14), .out15(demultiplexer_2_out15),
    .out16(demultiplexer_2_out16), .out17(demultiplexer_2_out17), .out18(demultiplexer_2_out18),
    .in(and_7_out), .sel(register_1_q[4:0]));  // open: out0, out19, out20, out21, out22, out23, out24, out25, out26, out27, out28, out29, out30, out31
  assign pull_resistor_2_node = and_8_out ? and_8_out : 1'bz;  // Controlled_Buffer controlled_buffer_11
  and and_8 (and_8_out, demultiplexer_2_out9, demultiplexer_1_out2);
  and and_9 (and_9_out, demultiplexer_1_out1, demultiplexer_2_out10);
  and and_10 (and_10_out, demultiplexer_2_out9, demultiplexer_1_out1);
  assign controlled_buffer_1_out = and_9_out ? multiplexer_2_out : 8'bz;  // Controlled_Buffer controlled_buffer_12
  and and_11 (and_11_out, demultiplexer_2_out10, demultiplexer_1_out2);
  and and_12 (and_12_out, demultiplexer_1_out1, demultiplexer_2_out11);
  buf buffer_15 (buffer_15_out, and_9_out);
  buf buffer_16 (buffer_16_out, and_11_out);
  buf buffer_17 (buffer_17_out, buffer_15_out);
  buf buffer_18 (buffer_18_out, buffer_16_out);
  assign controlled_buffer_2_out = and_9_out ? buffer_17_out : 1'bz;  // Controlled_Buffer controlled_buffer_13
  assign controlled_buffer_14_out = and_11_out ? buffer_18_out : 1'bz;  // Controlled_Buffer controlled_buffer_14
  assign controlled_buffer_15_out = and_11_out ? mmu_1_out_11 : 8'bz;  // Controlled_Buffer controlled_buffer_15
  and and_13 (and_13_out, demultiplexer_1_out1, demultiplexer_2_out12);
  and and_14 (and_14_out, demultiplexer_1_out1, demultiplexer_2_out13);
  and and_15 (and_15_out, demultiplexer_1_out1, demultiplexer_2_out14);
  // Priority_Encoder #(.select(2)) priority_encoder_2: pin names not known; wires that end beside it: and_13_out, and_14_out, priority_encoder_2_p3, and_15_out, priority_encoder_2_p5
  Pull_Resistor pull_resistor_4 (.node(priority_encoder_2_p3));
  buf buffer_19 (buffer_19_out, and_12_out);
  assign controlled_buffer_16_out = and_12_out ? register_3_q : 8'bz;  // Controlled_Buffer controlled_buffer_16
  and and_16 (priority_encoder_2_p5, demultiplexer_1_out1, demultiplexer_2_out15);
  or or_5 (or_5_out, demultiplexer_2_out15, demultiplexer_2_out14, demultiplexer_2_out13, demultiplexer_2_out12);
  assign bit_extender_1_out = {{1{priority_encoder_2_p3[1]}}, priority_encoder_2_p3};  // Bit_Extender bit_extender_1
  buf buffer_20 (buffer_20_out, buffer_19_out);
  assign controlled_buffer_17_out = and_12_out ? buffer_20_out : 1'bz;  // Controlled_Buffer controlled_buffer_17
  assign controlled_buffer_1_out = and_12_out ? multiplexer_2_out : 8'bz;  // Controlled_Buffer controlled_buffer_18
  and and_17 (and_17_out, rgbled_1_p1, register_1_q[7]);
  Demultiplexer #(.select(5)) demultiplexer_3 (
    .in(and_17_out), .sel(register_1_q[4:0]));  // open: out0, out1, out2, out3, out4, out5, out6, out7, out8, out9, out10, out11, out12, out13, out14, out15, out16, out17, out18, out19, out20, out21, out22, out23, out24, out25, out26, out27, out28, out29, out30, out31
  and and_18 (and_18_out, demultiplexer_2_out16, demultiplexer_1_out1);
  and and_19 (and_19_out, demultiplexer_2_out17, d_ff_2_q, demultiplexer_1_out1);
  or or_6 (or_6_out, and_18_out, and_19_out, and_21_out);
  and and_20 (and_20_out, demultiplexer_1_out2, or_5_out);
  buf buffer_21 (buffer_21_out, or_5_out);
  assign controlled_buffer_19_out = or_5_out ? multiplexer_2_out : 8'bz;  // Controlled_Buffer controlled_buffer_19
  assign controlled_buffer_20_out = or_5_out ? register_3_q : 8'bz;  // Controlled_Buffer controlled_buffer_20
  buf buffer_22 (buffer_22_out, buffer_21_out);
  buf buffer_23 (buffer_23_out, buffer_21_out);
  and and_21 (and_21_out, demultiplexer_2_out18, ~d_ff_2_q, demultiplexer_1_out1);  // AND_Gate
  assign controlled_buffer_21_out = or_5_out ? bit_extender_1_out : 3'bz;  // Controlled_Buffer controlled_buffer_21
  buf buffer_24 (buffer_24_out, and_20_out);
  buf buffer_25 (buffer_25_out, buffer_24_out);
  assign controlled_buffer_15_out = and_20_out ? register_2_q : 8'bz;  // Controlled_Buffer controlled_buffer_22
  assign controlled_buffer_14_out = buffer_25_out ? buffer_25_out : 1'bz;  // Controlled_Buffer controlled_buffer_23
  assign pull_resistor_1_node = or_6_out ? or_6_out : 1'bz;  // Controlled_Buffer controlled_buffer_24
  buf buffer_26 (buffer_26_out, or_6_out);
  buf buffer_27 (buffer_27_out, buffer_26_out);
  buf buffer_28 (buffer_28_out, buffer_27_out);
  assign controlled_buffer_25_out = buffer_28_out ? multiplexer_2_out : 8'bz;  // Controlled_Buffer controlled_buffer_25
  ROM #(.addrWidth(15)) rom_1 (.addr(mmu_1_romaddr), .data(rom_1_data));
  Pull_Resistor pull_resistor_5 (.node(controlled_buffer_2_out));
  Pull_Resistor pull_resistor_6 (.node(controlled_buffer_17_out));
  Pull_Resistor pull_resistor_7 (.node(controlled_buffer_6_out));
  assign controlled_buffer_14_out = demultiplexer_4_out0 ? demultiplexer_4_out0 : 1'bz;  // Controlled_Buffer controlled_buffer_26
  Demultiplexer #(.select(2)) demultiplexer_4 (
    .out0(demultiplexer_4_out0), .out1(demultiplexer_4_out1), .out2(demultiplexer_4_out2),
    .out3(demultiplexer_4_out3), .in(controlled_buffer_6_out), .sel(buffer_6_out));
  assign controlled_buffer_27_out = demultiplexer_4_out3 ? demultiplexer_4_out3 : 1'bz;  // Controlled_Buffer controlled_buffer_27
  D_Flip_Flop d_ff_2 (.D(alu_1_zero), .clk(buffer_22_out), .Q(d_ff_2_q));  // open: Qn, preset, reset
  MMU mmu_1 (
    .out_11(mmu_1_out_11), .ROMADDR(mmu_1_romaddr), .RAMBNK(controlled_buffer_3_out), .RAMBNKSET(and_2_out),
    .ROMBNK(controlled_buffer_4_out), .ROMBNKSET(and_3_out), .rst(and_4_out), .ADDR(controlled_buffer_1_out),
    .RD(controlled_buffer_2_out), .WRT(controlled_buffer_17_out), .VAL(controlled_buffer_16_out),
    .ROMOUT(rom_1_data));
  assign controlled_buffer_28_out = demultiplexer_4_out1 ? demultiplexer_4_out1 : 1'bz;  // Controlled_Buffer controlled_buffer_28
  assign controlled_buffer_29_out = demultiplexer_4_out2 ? demultiplexer_4_out2 : 1'bz;  // Controlled_Buffer controlled_buffer_29
  ALU alu_1 (
    .Sum(alu_1_sum), .Zero(alu_1_zero), .Carry(alu_1_carry), .Sel(controlled_buffer_21_out),
    .A(controlled_buffer_20_out), .B(controlled_buffer_19_out));
  D_Flip_Flop d_ff_3 (.D(alu_1_carry), .clk(buffer_22_out), .Q(d_ff_3_q));  // open: Qn, preset, reset
  Pull_Resistor pull_resistor_8 (.node(controlled_buffer_15_out));
  assign controlled_buffer_15_out = controlled_buffer_6_out ? controlled_buffer_5_out : 8'bz;  // Controlled_Buffer controlled_buffer_30
  Pull_Resistor pull_resistor_9 (.node(pull_resistor_9_node));
  assign pull_resistor_9_node = controlled_buffer_6_out ? controlled_buffer_5_out : 8'bz;  // Controlled_Buffer controlled_buffer_31
  Pull_Resistor pull_resistor_10 (.node(pull_resistor_10_node));
  assign pull_resistor_10_node = controlled_buffer_6_out ? controlled_buffer_5_out : 8'bz;  // Controlled_Buffer controlled_buffer_32
  Pull_Resistor pull_resistor_11 (.node(pull_resistor_11_node));
  assign pull_resistor_11_node = controlled_buffer_6_out ? controlled_buffer_5_out : 8'bz;  // Controlled_Buffer controlled_buffer_33
  Register #(.trigger("falling")) register_2 (.D(alu_1_sum), .Q(register_2_q), .clk(buffer_23_out));  // open: en, clr
  Pull_Resistor pull_resistor_12 (.node(controlled_buffer_14_out));
  Pull_Resistor pull_resistor_13 (.node(controlled_buffer_28_out));
  Pull_Resistor pull_resistor_14 (.node(controlled_buffer_29_out));
  Pull_Resistor pull_resistor_15 (.node(controlled_buffer_27_out));
  Register register_3 (
    .D(controlled_buffer_15_out), .Q(register_3_q), .clk(controlled_buffer_14_out), .clr(and_4_out));  // open: en
  Register register_4 (
    .D(pull_resistor_9_node), .Q(register_4_q), .clk(controlled_buffer_28_out), .clr(and_4_out));  // open: en
  Register register_5 (
    .D(pull_resistor_10_node), .Q(register_5_q), .clk(controlled_buffer_29_out), .clr(and_4_out));  // open: en
  Register register_6 (
    .D(pull_resistor_11_node), .Q(register_6_q), .clk(controlled_buffer_27_out), .clr(and_4_out));  // open: en
  Multiplexer #(.select(2), .width(8)) multiplexer_2 (
    .in0(register_3_q), .in1(register_4_q), .in2(register_5_q), .in3(register_6_q), .out(multiplexer_2_out),
    .sel(buffer_6_out));

  // Notes on the sheet:
  //   BRK
  //   TICK
  //   RED-FETCH
  //   GRN - EXEC
  //   STATE
  //   CONTINUE
  //   BNKROMV
  //   BNKRAMWRT
  //   BNKROMWRT
  //   PC
  //   BNKRAMV
  //   ADDR
  //   WRTVAL
  //   RD
  //   WR
  //   OUT
  //   WR_SEL_V
  //   WR_SEL
  //   SEL
  //   SEL_VAL
  //   A_VAL
  //   B_VAL
  //   C_VAL
  //   D_VAL
  //   WR_A_VAL
  //   WR_B_VAL
  //   WR_C_VAL
  //   WR_D_VAL
  //   WR_A
  //   WR_B
  //   WR_C
  //   WR_D
  //   ALU_A
  //   ALU_B
  //   ALU_Z
  //   ALU_C
  //   ALU_R
  //   ALU_S
  //   C_FLAG
  //   Z_FLAG
  //   FLAG
  //   FR_VAL
  //   FR
  //   skip pc
  //   t1/t2
  //   BANK
  //   RST
  //   STOP
  //   LD R,R
  //   LD R,V
  //   LD A,[R]
  //   LD [R],A
  //   ADD SUB MUL CMP
  //   JP
  //   Z
  //   NZ
  //   JUMP
  //   JADDR
  //   PC
  //   contents of rom_1 (hex, n*v repeats v):
  //   9 5 4 129*0 9 12 29 34 49 56 69 78 2 119*0 9 69 49 81 69 ff 4b 6b 9 0 29 0 6a 25 4a 2 112*0 9 69 29
  //   11 2c 65 2d 2 120*0 29 20 30 2 2 21*0 2 2 29 22 30 29*0 2 2 66*0 29 10 9 1 d 31 2 2 4*0 29 20 9 a 49
  //   1 4d 32 6*0 2 2 9 a 29 a 49 32 2f 51 6*0 4*2 9 34 10 2 2
  //   ALU FRZ register
  //   RST
endmodule

module MMU (
  input  [7:0] ROMOUT,
  input  rst,
  input  [7:0] RAMBNK,
  input  [7:0] ROMBNK,
  input  [7:0] ADDR,
  input  [7:0] VAL,
  input  RAMBNKSET,
  input  ROMBNKSET,
  input  RD,
  input  WRT,
  output [7:0] out_11,
  output [14:0] ROMADDR
);

  wire and_1_out, and_2_out, and_3_out, buffer_2_out, buffer_4_out, buffer_6_out, buffer_8_out, not_1_out,
       or_3_out;
  wire [7:0] buffer_1_out, buffer_3_out, buffer_5_out, buffer_7_out, multiplexer_1_out, ram_1_dout,
       register_1_q, register_2_q, undriven;
  wire [14:0] bit_extender_1_out, bit_extender_2_out, bit_extender_3_out, or_1_out, or_2_out, shifter_1_out,
       shifter_2_out;

  assign buffer_1_out = RAMBNK;  // Buffer buffer_1, 8 bits wide
  buf buffer_2 (buffer_2_out, RAMBNKSET);
  Pull_Resistor pull_resistor_1 (.node(RAMBNK));
  Pull_Resistor pull_resistor_2 (.node(RAMBNKSET));
  assign buffer_3_out = ROMBNK;  // Buffer buffer_3, 8 bits wide
  buf buffer_4 (buffer_4_out, ROMBNKSET);
  assign buffer_5_out = ADDR;  // Buffer buffer_5, 8 bits wide
  Pull_Resistor pull_resistor_3 (.node(ROMBNK));
  Pull_Resistor pull_resistor_4 (.node(ROMBNKSET));
  Pull_Resistor pull_resistor_5 (.node(ADDR));
  assign bit_extender_1_out = {{7{1'b0}}, register_1_q};  // Bit_Extender bit_extender_1
  Register register_1 (.D(buffer_1_out), .Q(register_1_q), .clk(buffer_2_out), .clr(rst));  // open: en
  assign bit_extender_2_out = {{8{1'b0}}, buffer_5_out[6:0]};  // Bit_Extender bit_extender_2
  assign bit_extender_3_out = {{7{1'b0}}, register_2_q};  // Bit_Extender bit_extender_3
  Register register_2 (.D(buffer_3_out), .Q(register_2_q), .clk(buffer_4_out), .clr(rst));  // open: en
  Shifter #(.width(15)) shifter_1 (.in(bit_extender_1_out), .\dist (4'b0111), .out(shifter_1_out));
  Shifter #(.width(15)) shifter_2 (.in(bit_extender_3_out), .\dist (4'b0111), .out(shifter_2_out));
  assign or_1_out = shifter_1_out | bit_extender_2_out;  // OR_Gate or_1, 15 bits wide
  assign or_2_out = bit_extender_2_out | shifter_2_out;  // OR_Gate or_2, 15 bits wide
  Register #(.trigger("high"), .width(15)) register_3 (.D(or_2_out), .Q(ROMADDR), .clk(and_3_out));  // open: en, clr
  and and_1 (and_1_out, buffer_5_out[7], or_3_out);
  and and_2 (and_2_out, buffer_5_out[7], buffer_8_out);
  or or_3 (or_3_out, buffer_6_out, buffer_8_out);
  buf buffer_6 (buffer_6_out, RD);
  Pull_Resistor pull_resistor_6 (.node(RD));
  RAM #(.addrWidth(15)) ram_1 (
    .addr(or_1_out), .we(and_2_out), .oe(and_1_out), .clk(and_1_out), .din(buffer_7_out), .dout(ram_1_dout));
  assign buffer_7_out = VAL;  // Buffer buffer_7, 8 bits wide
  Pull_Resistor pull_resistor_7 (.node(VAL));
  buf buffer_8 (buffer_8_out, WRT);
  Pull_Resistor pull_resistor_8 (.node(WRT));
  and and_3 (and_3_out, ~buffer_5_out[7], or_3_out);  // AND_Gate
  ErrorPullDown8 errorpulldown8_1 (.in_1({undriven[7], ram_1_dout[7], undriven[6], ram_1_dout[6], undriven[5], ram_1_dout[5], undriven[4], ram_1_dout[4], undriven[3], ram_1_dout[3], undriven[2], ram_1_dout[2], undriven[1], ram_1_dout[1], undriven[0], ram_1_dout[0]}));
  Multiplexer #(.width(8)) multiplexer_1 (.in0(undriven), .in1(ROMOUT), .out(multiplexer_1_out), .sel(not_1_out));
  not not_1 (not_1_out, buffer_5_out[7]);
  Register #(.trigger("high")) register_4 (.D(multiplexer_1_out), .Q(out_11), .clk(or_3_out));  // open: en, clr
endmodule

module ErrorPullDown8 (
  input  [7:0] in_1,
  output [7:0] out_2
);


  assign out_2 = in_1;

  // Notes on the sheet:
  //   out_2: pull=down
  //   in_1: pull=down
endmodule

module RisingEdge (
  input  in_1,
  output out_2
);

  wire not_1_out, not_2_out, not_3_out;

  not not_1 (not_1_out, in_1);
  and and_1 (out_2, in_1, not_2_out);
  not not_2 (not_2_out, not_3_out);
  not not_3 (not_3_out, not_1_out);
endmodule

module FallingEdge (
  input  in_1,
  output out_2
);

  wire buffer_1_out, not_1_out, not_2_out, not_3_out;

  buf buffer_1 (buffer_1_out, in_1);
  not not_1 (not_1_out, not_2_out);
  not not_2 (not_2_out, buffer_1_out);
  and and_1 (out_2, not_1_out, not_3_out);
  not not_3 (not_3_out, in_1);
endmodule

module ALU (
  input  [7:0] A,
  input  [7:0] B,
  input  [2:0] Sel,
  output [7:0] Sum,
  output Zero,
  output Carry
);

  wire adder_1_cout, subtractor_1_bout;
  wire [2:0] comparator_1_eq;
  wire [7:0] adder_1_out, bit_extender_1_out, multiplier_1_out, subtractor_1_out;

  assign Carry = adder_1_cout ? adder_1_cout : 1'bz;  // Controlled_Buffer controlled_buffer_1
  assign Carry = subtractor_1_bout ? subtractor_1_bout : 1'bz;  // Controlled_Buffer controlled_buffer_2
  Adder adder_1 (.a(A), .b(B), .out(adder_1_out), .cout(adder_1_cout));  // open: cin
  Subtractor subtractor_1 (.a(A), .b(B), .out(subtractor_1_out), .bout(subtractor_1_bout));  // open: bin
  Multiplier multiplier_1 (.a(A), .b(B), .out(multiplier_1_out));  // open: cin, cout
  Comparator #(.mode("unsigned")) comparator_1 (
    .a(A), .b(B), .gt(comparator_1_eq[1]), .eq(comparator_1_eq[0]), .lt(comparator_1_eq[2]));
  assign bit_extender_1_out = {{5{1'b0}}, comparator_1_eq};  // Bit_Extender bit_extender_1
  Multiplexer #(.select(3), .width(8)) multiplexer_1 (
    .in0(adder_1_out), .in1(subtractor_1_out), .in2(multiplier_1_out), .in3(bit_extender_1_out), .out(Sum),
    .sel(Sel));  // open: in4, in5, in6, in7
  Comparator #(.mode("unsigned")) comparator_2 (.a(Sum), .b({8{1'b0}}), .eq(Zero));  // open: gt, lt
endmodule

module testing (
);

  wire buffer_1_out, buffer_2_out, buffer_3_out, buffer_4_out, button_1_out, button_2_out, button_3_out,
       button_4_out, button_5_out, counter_1_carry, not_1_out, not_2_out, not_3_out, undriven;
  wire [7:0] mmu_1_out_11, rom_1_data, undriven_2, undriven_3, undriven_4, undriven_5;
  wire [14:0] mmu_1_romaddr;

  not not_1 (not_1_out, buffer_1_out);
  not not_2 (not_2_out, not_1_out);
  buf buffer_1 (buffer_1_out, undriven);
  not not_3 (not_3_out, undriven);
  // AND_Gate and_1 has open pins: in0=not_2_out, in1=not_3_out, out=open
  Button button_1 (.out(button_1_out));
  // DipSwitch dipswitch_1: pin names not known
  Button button_2 (.out(button_2_out));
  // DipSwitch dipswitch_2: pin names not known
  buf buffer_2 (buffer_2_out, button_1_out);
  buf buffer_3 (buffer_3_out, buffer_2_out);
  buf buffer_4 (buffer_4_out, buffer_3_out);
  // DipSwitch dipswitch_3: pin names not known
  Button button_3 (.out(button_3_out));
  // DipSwitch dipswitch_4: pin names not known
  Button button_4 (.out(button_4_out));
  Button button_5 (.out(button_5_out));
  Counter #(.trigger("falling")) counter_1 (
    .load(buffer_4_out), .clk(button_1_out), .D(8'h69), .carry(counter_1_carry));  // open: clr, up, count, Q
  ROM #(.addrWidth(15)) rom_1 (.addr(mmu_1_romaddr), .data(rom_1_data));
  DotMatrix #(.inputtype("row"), .matrixcols(8), .matrixrows(1)) dotmatrix_1 (.row0(mmu_1_out_11));
  MMU mmu_1 (
    .out_11(mmu_1_out_11), .ROMADDR(mmu_1_romaddr), .RAMBNK(undriven_2), .RAMBNKSET(button_2_out),
    .ROMBNK(undriven_3), .ROMBNKSET(button_3_out), .ADDR(undriven_4), .RD(button_4_out), .WRT(button_5_out),
    .VAL(undriven_5), .ROMOUT(rom_1_data));  // open: rst

  // Notes on the sheet:
  //   MMU TEST
endmodule
